// Logisim project Piloufas.circ as structural Verilog
module main (
);

  wire A_out, alarm__sound, B_out, C_out, home, home_1, home_2, home_3, nxt, nxt_1, nxt_2, nxt_3, or_1_out,
       or_2_out, or_4_out, or_5_out, or_6_out, rst_sys, second_clock_output_1;
  wire [3:0] display_o, display_o_2;
  wire [5:0] but_state, but_state_1, but_state_2, but_state_3, but_state_4;
  wire [23:0] D_alarm, D_chron, D_clock, D_timer;
  wire [23:8] display_o_3;

  Button A (.out(A_out));
  Button B (.out(B_out));
  Button C (.out(C_out));
  Button R (.out(rst_sys));
  Clock sysclk ();  // open: out
  buf or_1 (or_1_out, rst_sys);  // OR_Gate
  buf or_2 (or_2_out, rst_sys);  // OR_Gate
  button_input input_st_lg (.A(A_out), .B(B_out), .C(C_out), .but_o(but_state));  // open: R
  // Probe on but_state
  input_System button_switch (
    .b_i(but_state), .nxt(nxt), .R(or_1_out), .b_o_1(but_state_1), .b_o_2(but_state_2), .b_o_3(but_state_3),
    .b_o_4(but_state_4));
  // Probe on but_state_2
  // Probe on but_state_4
  alarmer alarm_ (
    .EN(1'b1), .R(or_2_out), .but_i(but_state_2), .t(D_clock), .o(D_alarm), .nxt(nxt_2), .rst(home_2),
    .sound(alarm__sound));
  LED LED_1 (.in(alarm__sound));
  or or_3 (home, home_1, home_2, home_3);
  or or_4 (or_4_out, home, rst_sys);
  output_display display (
    .i_1(D_clock), .i_2(D_alarm), .i_3(D_chron), .i_4(D_timer), .nxt(nxt), .R(or_4_out),
    .o({display_o_3, display_o_2, display_o}));
  time_div second_clock (.Output_1(second_clock_output_1));
  buf or_5 (or_5_out, rst_sys);  // OR_Gate
  Hex_Digit_Display hex_digit_display_1 (.value(display_o_3[23:20]));  // open: dp
  Hex_Digit_Display hex_digit_display_2 (.value(display_o_3[19:16]));  // open: dp
  buf or_6 (or_6_out, rst_sys);  // OR_Gate
  Hex_Digit_Display hex_digit_display_3 (.value(display_o_3[15:12]));  // open: dp
  // Probe on but_state_1
  // Probe on but_state_3
  or or_7 (nxt, nxt_1, nxt_2, nxt_3);
  Hex_Digit_Display hex_digit_display_4 (.value(display_o_3[11:8]));  // open: dp
  clocker2 clock_ (
    .EN(second_clock_output_1), .R(or_5_out), .but_i(but_state_1), .o(D_clock), .nxt(nxt_1), .rst(home_1));
  chronometer chron_ (.R(or_6_out), .b_i(but_state_3), .o(D_chron), .nxt(nxt_3), .rst(home_3));
  Hex_Digit_Display hex_digit_display_5 (.value(display_o));  // open: dp
  Hex_Digit_Display hex_digit_display_6 (.value(display_o_2));  // open: dp
endmodule

module press (
  input  b_in,
  input  R,
  output st,
  output lg
);

  wire Button_1_out, clock_1_out, not_1_out, not_2_out, or_1_out, undriven;

  Button Button_1 (.out(Button_1_out));
  Clock clock_1 (.out(clock_1_out));
  or or_1 (or_1_out, b_in, Button_1_out);
  not not_1 (not_1_out, undriven);
  // NOT_Gate not_2 has open pins: in=open, out=not_2_out
  buf and_1 (st, not_1_out);  // AND_Gate
  and and_2 (lg, undriven, not_2_out);
endmodule

module button_input (
  input  A,
  input  B,
  input  C,
  input  R,
  output [5:0] but_o
);

  press press_A (.b_in(A), .R(R), .st(but_o[0]), .lg(but_o[1]));
  press press_B (.b_in(B), .R(R), .st(but_o[2]), .lg(but_o[3]));
  press press_C (.b_in(C), .R(R), .st(but_o[4]), .lg(but_o[5]));

  // Notes on the sheet:
  //   Dans l'ordre de 0 à 5 : A_st | A_lg | B_st | B_lg | C_st | C_lg
endmodule

module output_display (
  input  [23:0] i_1,
  input  [23:0] i_2,
  input  [23:0] i_3,
  input  [23:0] i_4,
  input  nxt,
  input  R,
  output [23:0] o
);

  wire clock_1_out;
  wire [1:0] undriven;

  Clock clock_1 (.out(clock_1_out));
  Multiplexer #(.select(2), .width(24), .enable("false")) multiplexer_1 (
    .in0(i_1), .in1(i_2), .in2(i_3), .in3(i_4), .out(o), .sel(undriven));
endmodule

module count_to_sixty (
  input  EN,
  input  R,
  output [3:0] low,
  output [3:0] high,
  output c
);

  wire and_1_out, clock_1_out, counter_1_carry, counter_2_carry;

  Clock clock_1 (.out(clock_1_out));
  Counter #(.width(4), .max('h9)) counter_1 (
    .clr(R), .count(EN), .clk(clock_1_out), .carry(counter_1_carry), .Q(low));  // open: load, up, D
  Counter #(.width(4), .max('h5)) counter_2 (
    .clr(R), .count(and_1_out), .clk(clock_1_out), .carry(counter_2_carry), .Q(high));  // open: load, up, D
  and and_1 (and_1_out, counter_1_carry, EN);
  and and_2 (c, counter_2_carry, and_1_out);
endmodule

module count_to_twenty (
  input  EN,
  input  R,
  output [3:0] low,
  output [3:0] high
);

  wire and_1_out, and_2_out, clock_1_out, comparator_1_eq, counter_1_carry, counter_2_carry, or_1_out;

  Clock clock_1 (.out(clock_1_out));
  or or_1 (or_1_out, R, and_2_out);
  Counter #(.width(4), .max('h9)) counter_1 (
    .clr(or_1_out), .count(EN), .clk(clock_1_out), .carry(counter_1_carry), .Q(low));  // open: load, up, D
  Counter #(.width(4), .max('h2)) counter_2 (
    .clr(or_1_out), .count(and_1_out), .clk(clock_1_out), .carry(counter_2_carry), .Q(high));  // open: load, up, D
  and and_1 (and_1_out, counter_1_carry, EN);
  Comparator #(.width(4)) comparator_1 (.a(low), .b(4'b0100), .eq(comparator_1_eq));  // open: gt, lt
  and and_2 (and_2_out, comparator_1_eq, counter_2_carry);
endmodule

module clocker (
  input  EN,
  input  R,
  output [23:0] o
);

  wire count_to_sixty_1_c, count_to_sixty_2_c;

  count_to_sixty count_to_sixty_1 (.EN(EN), .R(R), .low(o[3:0]), .high(o[7:4]), .c(count_to_sixty_1_c));
  count_to_sixty count_to_sixty_2 (
    .EN(count_to_sixty_1_c), .R(R), .low(o[11:8]), .high(o[15:12]), .c(count_to_sixty_2_c));
  count_to_twenty count_to_twenty_1 (.EN(count_to_sixty_2_c), .R(R), .low(o[19:16]), .high(o[23:20]));
endmodule

module input_System (
  input  [5:0] b_i,
  input  nxt,
  input  R,
  output [5:0] b_o_1,
  output [5:0] b_o_2,
  output [5:0] b_o_3,
  output [5:0] b_o_4
);

  wire clock_1_out;
  wire [1:0] counter_1_q;

  Clock clock_1 (.out(clock_1_out));
  Counter #(.width(2), .max('h3)) counter_1 (
    .clr(R), .count(nxt), .clk(clock_1_out), .Q(counter_1_q));  // open: load, up, D, carry
  Demultiplexer #(.select(2), .width(6), .enable("false")) demultiplexer_1 (
    .out0(b_o_1), .out1(b_o_2), .out2(b_o_3), .out3(b_o_4), .in(b_i), .sel(counter_1_q));
endmodule

module clocker2 (
  input  EN,
  input  R,
  input  [5:0] but_i,
  output [23:0] o,
  output nxt,
  output rst
);

  wire and_1_out;

  Clock clock_1 ();  // open: out
  and and_1 (and_1_out, EN, R);
  LED test (.in(and_1_out));
  or or_1 (nxt, but_i[2], but_i[3]);

  assign o = 24'h12345;
  assign rst = 1'b0;
endmodule

module alarmer (
  input  EN,
  input  R,
  input  [5:0] but_i,
  input  [23:0] t,
  output [23:0] o,
  output nxt,
  output rst,
  output sound
);

  Clock clock_1 ();  // open: out
  or or_1 (nxt, but_i[2], but_i[3]);

  assign rst = 1'b0;
  assign sound = 1'b0;
endmodule

module chronometer (
  input  R,
  input  [5:0] b_i,
  output [23:0] o,
  output nxt,
  output rst
);

  wire A, and_1_out, B, C, centieme_c, chron_div_1_output_1, clock_1_out, d_ff_1_q, dixieme_c, or_1_out,
       or_5_out, seconds_c, start;

  chron_div chron_div_1 (.Output_1(chron_div_1_output_1));
  or or_1 (or_1_out, R, A);
  or or_2 (A, b_i[0], b_i[1]);
  or or_3 (B, b_i[2], b_i[3]);
  or or_4 (C, b_i[4], b_i[5]);
  and and_1 (and_1_out, start, chron_div_1_output_1);
  count_to_ten centieme (.EN(and_1_out), .R(or_1_out), .o(o[3:0]), .c(centieme_c));
  count_to_ten dixieme (.EN(centieme_c), .R(or_1_out), .o(o[7:4]), .c(dixieme_c));
  count_to_sixty seconds (.EN(dixieme_c), .R(or_1_out), .low(o[11:8]), .high(o[15:12]), .c(seconds_c));
  count_to_sixty minutes (.EN(seconds_c), .R(or_1_out), .low(o[19:16]), .high(o[23:20]));  // open: c
  T_Flip_Flop t_ff_1 (.T(C), .clk(clock_1_out), .Q(start));  // open: Qn, reset, preset
  Clock clock_1 (.out(clock_1_out));
  or or_5 (or_5_out, A, C);
  D_Flip_Flop d_ff_1 (.Q(d_ff_1_q), .preset(or_5_out), .reset(R));  // open: D, clk, Qn
  and and_2 (nxt, B, ~d_ff_1_q);  // AND_Gate
  and and_3 (rst, d_ff_1_q, B);

  // Other names for the same wires on the sheet: rst_t = R

  // Notes on the sheet:
  //   précision au centieme
endmodule

module count_to_ten (
  input  EN,
  input  R,
  output [3:0] o,
  output c
);

  wire counter_1_carry;

  Clock clock_1 ();  // open: out
  Counter #(.width(4), .max('h9)) counter_1 (
    .clr(R), .count(EN), .clk(EN), .carry(counter_1_carry), .Q(o));  // open: load, up, D
  and and_1 (c, EN, counter_1_carry);
endmodule

module time_div (
  output Output_1
);

  wire clock_1_out, divide_four_1_o;

  Clock clock_1 (.out(clock_1_out));
  divide_four divide_four_1 (.o(divide_four_1_o));
  LED LED_1 (.in(divide_four_1_o));
  divide_four divide_four_2 ();  // open: o
  divide_four divide_four_3 ();  // open: o
  divide_two divide_two_1 ();
endmodule

module chron_div (
  output Output_1
);

  Clock clk (.out(Output_1));
endmodule

module divide_four (
  output o
);

  wire clock_1_out, d_ff_1_q, d_ff_2_q, d_ff_3_q;

  Clock clock_1 (.out(clock_1_out));
  D_Flip_Flop d_ff_1 (.D(o), .clk(clock_1_out), .Q(d_ff_1_q));  // open: Qn, preset, reset
  D_Flip_Flop d_ff_2 (.D(d_ff_1_q), .clk(clock_1_out), .Q(d_ff_2_q), .reset(o));  // open: Qn, preset
  D_Flip_Flop d_ff_3 (.D(d_ff_2_q), .clk(clock_1_out), .Q(d_ff_3_q), .reset(o));  // open: Qn, preset
  D_Flip_Flop d_ff_4 (.D(d_ff_3_q), .clk(clock_1_out), .Q(o));  // open: Qn, preset, reset
endmodule

module full_adder (
  input  i_in,
  input  c_in,
  output val,
  output c_out
);
endmodule
