// Logisim project additionner_syslog.circ as structural Verilog
module bit_counter (
  input  In3,
  input  In4
);

  wire [1:0] clock_1_out;

  Clock clock_1 (.out(clock_1_out[0]));
  Clock clock_2 (.out(clock_1_out[1]));
  Hex_Digit_Display hex_digit_display_1 (.value({In4, In3, clock_1_out}));  // open: dp
endmodule

module one_digit_display (
);

  wire additionner_0_9_1_c_out, additionner_0_9_2_c_out, additionneur_0_5_1_c_out, clock_1_out;
  wire [3:0] additionner_0_9_1_one, additionner_0_9_2_one, additionneur_0_5_1_one, additionneur_0_5_2_one;

  Clock clock_1 (.out(clock_1_out));
  additionner_0_9 additionner_0_9_1 (
    .CLK_input(clock_1_out), .c_out(additionner_0_9_1_c_out), .one(additionner_0_9_1_one[0]),
    .two(additionner_0_9_1_one[1]), .four(additionner_0_9_1_one[2]), .eight(additionner_0_9_1_one[3]));
  additionneur_0_5 additionneur_0_5_1 (
    .CLK_input(additionner_0_9_1_c_out), .c_out(additionneur_0_5_1_c_out), .one(additionneur_0_5_1_one[0]),
    .two(additionneur_0_5_1_one[1]), .four(additionneur_0_5_1_one[2]));
  not not_1 (additionneur_0_5_1_one[3], 1'b1);
  additionner_0_9 additionner_0_9_2 (
    .CLK_input(additionneur_0_5_1_c_out), .c_out(additionner_0_9_2_c_out), .one(additionner_0_9_2_one[0]),
    .two(additionner_0_9_2_one[1]), .four(additionner_0_9_2_one[2]), .eight(additionner_0_9_2_one[3]));
  additionneur_0_5 additionneur_0_5_2 (
    .CLK_input(additionner_0_9_2_c_out), .one(additionneur_0_5_2_one[0]), .two(additionneur_0_5_2_one[1]),
    .four(additionneur_0_5_2_one[2]));  // open: c_out
  not not_2 (additionneur_0_5_2_one[3], 1'b1);
  Hex_Digit_Display hex_digit_display_1 (.value(additionner_0_9_1_one));  // open: dp
  Hex_Digit_Display hex_digit_display_2 (.value(additionneur_0_5_1_one));  // open: dp
  Hex_Digit_Display hex_digit_display_3 (.value(additionner_0_9_2_one));  // open: dp
  Hex_Digit_Display hex_digit_display_4 (.value(additionneur_0_5_2_one));  // open: dp
endmodule

module divide_by_2 (
  input  clock_input,
  output ou1
);

  wire d_ff_1_q, d_ff_1_qn;

  D_Flip_Flop d_ff_1 (.D(d_ff_1_qn), .clk(clock_input), .Q(d_ff_1_q), .Qn(d_ff_1_qn));  // open: preset, reset
  not not_1 (ou1, d_ff_1_q);
endmodule

module divide_by_4 (
  input  clock_input,
  output ou2
);

  wire d_ff_1_q, d_ff_1_qn, d_ff_2_qn;

  D_Flip_Flop d_ff_1 (.D(d_ff_1_qn), .clk(clock_input), .Q(d_ff_1_q), .Qn(d_ff_1_qn));  // open: preset, reset
  D_Flip_Flop d_ff_2 (.D(d_ff_2_qn), .clk(d_ff_1_q), .Q(ou2), .Qn(d_ff_2_qn));  // open: preset, reset
endmodule

module divide_by_8 (
  input  clock_input,
  output ou3
);

  wire d_ff_1_q, d_ff_1_qn, d_ff_2_q, d_ff_2_qn, d_ff_3_q, d_ff_3_qn;

  D_Flip_Flop d_ff_1 (.D(d_ff_1_qn), .clk(clock_input), .Q(d_ff_1_q), .Qn(d_ff_1_qn));  // open: preset, reset
  D_Flip_Flop d_ff_2 (.D(d_ff_2_qn), .clk(d_ff_1_q), .Q(d_ff_2_q), .Qn(d_ff_2_qn));  // open: preset, reset
  D_Flip_Flop d_ff_3 (.D(d_ff_3_qn), .clk(d_ff_2_q), .Q(d_ff_3_q), .Qn(d_ff_3_qn));  // open: preset, reset
  not not_1 (ou3, d_ff_3_q);
endmodule

module additionner_0_9 (
  input  CLK_input,
  output c_out,
  output one,
  output two,
  output four,
  output eight
);

  wire and_1_out, and_2_out, d_ff_1_qn, j_k_ff_1_q, j_k_ff_2_q, j_k_ff_3_q, not_1_out, not_2_out, not_3_out,
       not_4_out, undriven;

  J_K_Flip_Flop j_k_ff_1 (
    .J(1'b1), .K(1'b1), .clk(CLK_input), .Q(j_k_ff_1_q), .Qn(one), .preset(and_1_out));  // open: reset
  J_K_Flip_Flop j_k_ff_2 (
    .J(1'b1), .K(1'b1), .clk(j_k_ff_1_q), .Q(j_k_ff_2_q), .Qn(two), .preset(and_1_out), .reset(undriven));
  J_K_Flip_Flop j_k_ff_3 (
    .J(1'b1), .K(1'b1), .clk(j_k_ff_2_q), .Q(j_k_ff_3_q), .Qn(four), .preset(and_1_out));  // open: reset
  not not_1 (not_1_out, j_k_ff_2_q);
  J_K_Flip_Flop j_k_ff_4 (.J(1'b1), .K(1'b1), .clk(j_k_ff_3_q), .Qn(eight), .preset(and_1_out));  // open: Q, reset
  and and_1 (and_1_out, not_1_out, eight);
  not not_2 (not_2_out, two);
  not not_3 (not_3_out, four);
  not not_4 (not_4_out, eight);
  D_Flip_Flop d_ff_1 (.D(d_ff_1_qn), .clk(and_1_out), .Q(c_out), .Qn(d_ff_1_qn), .reset(and_2_out));  // open: preset
  and and_2 (and_2_out, one, not_2_out, not_3_out, not_4_out);
endmodule

module additionneur_0_5 (
  input  CLK_input,
  output c_out,
  output one,
  output two,
  output four
);

  wire and_1_out, and_2_out, d_ff_1_qn, j_k_ff_1_q, j_k_ff_2_q, not_1_out, not_2_out, undriven;

  J_K_Flip_Flop j_k_ff_1 (
    .J(1'b1), .K(1'b1), .clk(CLK_input), .Q(j_k_ff_1_q), .Qn(one), .preset(and_1_out));  // open: reset
  J_K_Flip_Flop j_k_ff_2 (
    .J(1'b1), .K(1'b1), .clk(j_k_ff_1_q), .Q(j_k_ff_2_q), .Qn(two), .preset(and_1_out), .reset(undriven));
  J_K_Flip_Flop j_k_ff_3 (.J(1'b1), .K(1'b1), .clk(j_k_ff_2_q), .Qn(four), .preset(and_1_out));  // open: Q, reset
  and and_1 (and_1_out, two, four);
  not not_1 (not_1_out, two);
  not not_2 (not_2_out, four);
  D_Flip_Flop d_ff_1 (.D(d_ff_1_qn), .clk(and_1_out), .Q(c_out), .Qn(d_ff_1_qn), .reset(and_2_out));  // open: preset
  and and_2 (and_2_out, one, not_1_out, not_2_out);
endmodule
