// Logisim project time.circ as structural Verilog: 12 circuits, main circuit seconds_counter
module seconds_counter (
  input  run_wk_s,
  input  CLK_input,
  input  run_st_s,
  input  set_mode,
  output [3:0] s1_output,
  output s_c_out,
  output [3:0] s2_output
);

  wire and_1_out, and_3_out, and_5_out, not_1_out, or_1_out, out_1, out_2;

  not not_1 (not_1_out, set_mode);
  or or_1 (or_1_out, run_st_s, and_1_out);
  and and_1 (and_1_out, out_1, not_1_out);
  and and_2 (out_1, s1_output[0], s1_output[3]);
  and and_3 (and_3_out, s1_output[1], s1_output[3]);
  add_4_bits add_4_bits_1 (.enable(run_wk_s), .CLK_input(CLK_input), .Reset(and_3_out), .out_put(s1_output));
  and and_4 (s_c_out, out_1, and_5_out);
  add_4_bits add_4_bits_2 (.enable(or_1_out), .CLK_input(CLK_input), .Reset(out_2), .out_put(s2_output));
  and and_5 (and_5_out, s2_output[0], s2_output[2]);
  and and_6 (out_2, s2_output[1], s2_output[2]);

  // Other names for the same wires on the sheet: c_out = s_c_out
endmodule

module date (
  input  set_mode,
  input  but_in,
  input  CLK_input,
  input  next_digit,
  output nv_jour
);

  wire and_1_out, and_2_out, and_3_out, and_4_out, and_5_out, and_6_out, and_7_out, demultiplexer_1_out0,
       demultiplexer_1_out1, demultiplexer_1_out2, demultiplexer_1_out3, demultiplexer_1_out4,
       demultiplexer_1_out5, demultiplexer_1_out6, minutes_counter_1_c_out, not_1_out, not_2_out, or_1_out,
       or_2_out, seconds_counter_1_s_c_out, t_ff_1_q;
  wire [2:0] add_4_bits_1_out_put;
  wire [3:0] hours_counter_1_st_hr, hours_counter_1_wk_hr, minutes_counter_1_m1_out,
       minutes_counter_1_m2_out, multiplexer_1_out, multiplexer_2_out, multiplexer_3_out, multiplexer_4_out,
       multiplexer_5_out, multiplexer_6_out, seconds_counter_1_s1_output, seconds_counter_1_s2_output;
  wire [3:3] add_4_bits_1_out_put_2;

  T_Flip_Flop t_ff_1 (.T(set_mode), .clk(CLK_input), .Q(t_ff_1_q));  // open: Qn, reset, preset
  Demultiplexer #(.select(3), .enable("false")) demultiplexer_1 (
    .out0(demultiplexer_1_out0), .out1(demultiplexer_1_out1), .out2(demultiplexer_1_out2),
    .out3(demultiplexer_1_out3), .out4(demultiplexer_1_out4), .out5(demultiplexer_1_out5),
    .out6(demultiplexer_1_out6), .in(t_ff_1_q), .sel(add_4_bits_1_out_put));  // open: out7
  and and_1 (and_1_out, t_ff_1_q, but_in, demultiplexer_1_out0);
  add_4_bits add_4_bits_1 (
    .enable(next_digit), .CLK_input(CLK_input), .Reset(demultiplexer_1_out6),
    .out_put({add_4_bits_1_out_put_2[3], add_4_bits_1_out_put}));
  not not_1 (not_1_out, t_ff_1_q);
  or or_1 (or_1_out, not_1_out, and_1_out);
  and and_2 (and_2_out, t_ff_1_q, but_in, demultiplexer_1_out1);
  and and_3 (and_3_out, t_ff_1_q, but_in, demultiplexer_1_out2);
  and and_4 (and_4_out, t_ff_1_q, but_in, demultiplexer_1_out3);
  and and_5 (and_5_out, t_ff_1_q, but_in, demultiplexer_1_out4);
  and and_6 (and_6_out, t_ff_1_q, but_in, demultiplexer_1_out5);
  not not_2 (not_2_out, t_ff_1_q);
  and and_7 (and_7_out, CLK_input, t_ff_1_q);
  or or_2 (or_2_out, not_2_out, and_7_out);
  seconds_counter seconds_counter_1 (
    .run_wk_s(or_1_out), .CLK_input(CLK_input), .run_st_s(and_2_out), .set_mode(t_ff_1_q),
    .s1_output(seconds_counter_1_s1_output), .s_c_out(seconds_counter_1_s_c_out),
    .s2_output(seconds_counter_1_s2_output));
  minutes_counter minutes_counter_1 (
    .run_wk_mn(and_3_out), .c_in(seconds_counter_1_s_c_out), .CLK_input(CLK_input), .run_st_mn(and_4_out),
    .m1_out(minutes_counter_1_m1_out), .m2_out(minutes_counter_1_m2_out), .c_out(minutes_counter_1_c_out));
  hours_counter hours_counter_1 (
    .run_st_hr(and_6_out), .run_wk_hr(and_5_out), .CLK_input(CLK_input), .c_in_m(minutes_counter_1_c_out),
    .c_in_s(seconds_counter_1_s_c_out), .set_mode(t_ff_1_q), .c_out(nv_jour), .st_hr(hours_counter_1_st_hr),
    .wk_hr(hours_counter_1_wk_hr));
  Hex_Digit_Display hex_digit_display_1 (.value(multiplexer_1_out));  // open: dp
  Hex_Digit_Display hex_digit_display_2 (.value(multiplexer_2_out));  // open: dp
  Multiplexer #(.width(4), .enable("false")) multiplexer_1 (
    .in1(hours_counter_1_st_hr), .out(multiplexer_1_out), .sel(or_2_out));  // open: in0
  Multiplexer #(.width(4), .enable("false")) multiplexer_2 (
    .in1(hours_counter_1_wk_hr), .out(multiplexer_2_out), .sel(or_2_out));  // open: in0
  Hex_Digit_Display hex_digit_display_3 (.value(multiplexer_3_out));  // open: dp
  Multiplexer #(.width(4), .enable("false")) multiplexer_3 (
    .in1(minutes_counter_1_m2_out), .out(multiplexer_3_out), .sel(or_2_out));  // open: in0
  Hex_Digit_Display hex_digit_display_4 (.value(multiplexer_4_out));  // open: dp
  Multiplexer #(.width(4), .enable("false")) multiplexer_4 (
    .in1(minutes_counter_1_m1_out), .out(multiplexer_4_out), .sel(or_2_out));  // open: in0
  Hex_Digit_Display hex_digit_display_5 (.value(multiplexer_5_out));  // open: dp
  Multiplexer #(.width(4), .enable("false")) multiplexer_5 (
    .in1(seconds_counter_1_s2_output), .out(multiplexer_5_out), .sel(or_2_out));  // open: in0
  Hex_Digit_Display hex_digit_display_6 (.value(multiplexer_6_out));  // open: dp
  Multiplexer #(.width(4), .enable("false")) multiplexer_6 (
    .in1(seconds_counter_1_s1_output), .out(multiplexer_6_out), .sel(or_2_out));  // open: in0

  // Notes on the sheet:
  //   flip floop
  //   flip floop
  //   fix 29 in set mode
endmodule

module minutes_counter (
  input  run_wk_mn,
  input  c_in,
  input  CLK_input,
  input  run_st_mn,
  output [3:0] m1_out,
  output [3:0] m2_out,
  output c_out
);

  wire and_1_out, and_4_out, and_5_out, or_1_out, or_2_out, out_4, out_5;

  and and_1 (and_1_out, c_in, out_4);
  or or_1 (or_1_out, run_wk_mn, c_in);
  or or_2 (or_2_out, run_st_mn, and_1_out);
  and and_2 (c_out, out_4, and_5_out);
  and and_3 (out_4, m1_out[3], m1_out[0]);
  and and_4 (and_4_out, m1_out[3], m1_out[1]);
  add_4_bits add_4_bits_1 (.enable(or_1_out), .CLK_input(CLK_input), .Reset(and_4_out), .out_put(m1_out));
  and and_5 (and_5_out, m2_out[0], m2_out[2]);
  add_4_bits add_4_bits_2 (.enable(or_2_out), .CLK_input(CLK_input), .Reset(out_5), .out_put(m2_out));
  and and_6 (out_5, m2_out[2], m2_out[1]);

  // Notes on the sheet:
  //   is c_in alright ?
endmodule

module hours_counter (
  input  run_st_hr,
  input  run_wk_hr,
  input  CLK_input,
  input  c_in_m,
  input  c_in_s,
  input  set_mode,
  output c_out,
  output [3:0] st_hr,
  output [3:0] wk_hr
);

  wire and_1_out, and_2_out, and_4_out, and_5_out, and_6_out, and_9_out, incr_1, incr_2, not_1_out, or_1_out,
       or_2_out, or_3_out, or_4_out, out_6, out_7, reset, reset_impulse;

  not not_1 (not_1_out, set_mode);
  and and_1 (and_1_out, and_2_out, incr_2);
  and and_2 (and_2_out, c_in_m, c_in_s, not_1_out);
  or or_1 (or_1_out, reset, reset_impulse, out_7);
  or or_2 (or_2_out, run_st_hr, and_1_out);
  or or_3 (or_3_out, reset, reset_impulse, out_6);
  or or_4 (or_4_out, run_wk_hr, and_2_out);
  add_4_bits add_4_bits_1 (.enable(or_2_out), .CLK_input(CLK_input), .Reset(or_1_out), .out_put(st_hr));
  add_4_bits add_4_bits_2 (.enable(or_4_out), .CLK_input(CLK_input), .Reset(or_3_out), .out_put(wk_hr));
  hours_conditions hours_conditions_1 (.wk_hours_input(wk_hr), .st_hours_input(st_hr), .reset_impulse(reset_impulse));
  or or_5 (reset, and_4_out, and_5_out, and_6_out);
  and and_3 (out_7, st_hr[0], st_hr[1]);
  and and_4 (and_4_out, wk_hr[2], st_hr[1]);
  and and_5 (and_5_out, st_hr[1], st_hr[0], wk_hr[3]);
  and and_6 (and_6_out, st_hr[1], wk_hr[0], wk_hr[2]);
  and and_7 (out_6, wk_hr[1], wk_hr[3]);
  and and_8 (c_out, st_hr[1], c_in_m, and_9_out, c_in_s);
  and and_9 (and_9_out, wk_hr[1], wk_hr[0]);
  and and_10 (incr_1, wk_hr[3], wk_hr[1]);
  and and_11 (incr_2, wk_hr[0], wk_hr[3]);

  // Notes on the sheet:
  //   add conditions to fix anything above 23
endmodule

module add_4_bits (
  input  enable,
  input  CLK_input,
  input  Reset,
  output [3:0] out_put
);

  wire and_1_out, and_2_out, and_3_out, and_4_out, and_5_out;

  J_K_Flip_Flop j_k_ff_1 (.J(enable), .K(enable), .clk(CLK_input), .Q(out_put[0]), .reset(Reset));  // open: Qn, preset
  J_K_Flip_Flop j_k_ff_2 (
    .J(and_1_out), .K(and_1_out), .clk(CLK_input), .Q(out_put[1]), .reset(Reset));  // open: Qn, preset
  and and_1 (and_1_out, enable, out_put[0]);
  and and_2 (and_2_out, out_put[1], out_put[0]);
  and and_3 (and_3_out, enable, and_2_out);
  J_K_Flip_Flop j_k_ff_3 (
    .J(and_3_out), .K(and_3_out), .clk(CLK_input), .Q(out_put[2]), .reset(Reset));  // open: Qn, preset
  and and_4 (and_4_out, and_2_out, out_put[2]);
  J_K_Flip_Flop j_k_ff_4 (
    .J(and_5_out), .K(and_5_out), .clk(CLK_input), .Q(out_put[3]), .reset(Reset));  // open: Qn, preset
  and and_5 (and_5_out, enable, and_4_out);

  // Other names for the same wires on the sheet: EN = enable
endmodule

module mid_letter (
  input  A,
  input  B,
  input  C,
  input  D,
  output cnt,
  output lft_high,
  output top,
  output right_h,
  output left_bt,
  output bt,
  output right_bt
);

  wire and_1_out, and_2_out, and_3_out, and_4_out, and_5_out, and_6_out, and_7_out, and_8_out, and_9_out,
       and_10_out, and_11_out, and_12_out, and_13_out, and_14_out, and_15_out, and_16_out, and_17_out,
       and_18_out, and_19_out, and_20_out, and_21_out, and_22_out, and_23_out, and_24_out, and_25_out,
       and_26_out, and_27_out, and_28_out, not_1_out, not_2_out, not_3_out, not_4_out, not_5_out, not_6_out,
       not_7_out, not_8_out, not_9_out, not_10_out, not_11_out, not_12_out, not_13_out, not_14_out,
       not_15_out, not_16_out, not_17_out, not_18_out, not_19_out, not_20_out, not_21_out, not_22_out,
       not_23_out, not_24_out, not_25_out, not_26_out, not_27_out, not_28_out, not_29_out, not_30_out,
       not_31_out, not_32_out, not_33_out, not_34_out, not_35_out, not_36_out, not_37_out;

  not not_1 (not_1_out, C);
  and and_1 (and_1_out, not_1_out, D);
  not not_2 (not_2_out, A);
  and and_2 (and_2_out, not_2_out, not_3_out, C);
  not not_3 (not_3_out, B);
  and and_3 (and_3_out, A, B, not_4_out);
  not not_4 (not_4_out, C);
  not not_5 (not_5_out, A);
  and and_4 (and_4_out, not_5_out, D);
  not not_6 (not_6_out, A);
  and and_5 (and_5_out, not_6_out, C);
  not not_7 (not_7_out, A);
  and and_6 (and_6_out, not_7_out, B);
  and and_7 (and_7_out, A, not_8_out);
  not not_8 (not_8_out, B);
  and and_8 (and_8_out, A, not_9_out, not_10_out);
  not not_9 (not_9_out, C);
  not not_10 (not_10_out, D);
  not not_11 (not_11_out, C);
  and and_9 (and_9_out, not_11_out, D);
  not not_12 (not_12_out, B);
  and and_10 (and_10_out, not_12_out, C);
  and and_11 (and_11_out, A, B, not_13_out);
  not not_13 (not_13_out, C);
  not not_14 (not_14_out, A);
  not not_15 (not_15_out, B);
  not not_16 (not_16_out, A);
  not not_17 (not_17_out, B);
  not not_18 (not_18_out, C);
  not not_19 (not_19_out, D);
  not not_20 (not_20_out, A);
  and and_12 (and_12_out, not_20_out, D);
  not not_21 (not_21_out, A);
  and and_13 (and_13_out, not_21_out, C);
  not not_22 (not_22_out, A);
  and and_14 (and_14_out, not_22_out, B);
  and and_15 (and_15_out, A, not_23_out);
  not not_23 (not_23_out, B);
  and and_16 (and_16_out, A, not_24_out, not_25_out);
  not not_24 (not_24_out, C);
  not not_25 (not_25_out, D);
  not not_26 (not_26_out, A);
  and and_17 (and_17_out, not_26_out, C, not_27_out);
  not not_27 (not_27_out, D);
  and and_18 (and_18_out, B, not_28_out, not_29_out);
  not not_28 (not_28_out, C);
  not not_29 (not_29_out, D);
  not not_30 (not_30_out, A);
  and and_19 (and_19_out, not_30_out, B, C);
  and and_20 (and_20_out, A, not_31_out);
  not not_31 (not_31_out, B);
  not not_32 (not_32_out, A);
  not not_33 (not_33_out, B);
  not not_34 (not_34_out, A);
  not not_35 (not_35_out, B);
  not not_36 (not_36_out, C);
  not not_37 (not_37_out, D);
  or or_1 (cnt, and_1_out, and_2_out, and_3_out);
  or or_2 (lft_high, and_4_out, and_5_out, and_6_out, and_7_out, and_8_out);
  or or_3 (top, and_9_out, and_10_out, and_11_out);
  and and_21 (and_21_out, not_14_out, D);
  and and_22 (and_22_out, not_15_out, C, D);
  and and_23 (and_23_out, not_16_out, B);
  and and_24 (and_24_out, A, not_17_out, not_18_out, not_19_out);
  or or_4 (left_bt, and_12_out, and_13_out, and_14_out, and_15_out, and_16_out);
  or or_5 (bt, and_17_out, and_18_out, and_19_out, and_20_out);
  and and_25 (and_25_out, not_32_out, D);
  and and_26 (and_26_out, not_33_out, C, D);
  and and_27 (and_27_out, not_34_out, B);
  and and_28 (and_28_out, A, not_35_out, not_36_out, not_37_out);
  or or_6 (right_h, and_21_out, and_22_out, and_23_out, and_24_out);
  or or_7 (right_bt, and_25_out, and_26_out, and_27_out, and_28_out);
endmodule

module fst_letter (
  input  A,
  input  B,
  input  C,
  input  D,
  output cnt,
  output left_h,
  output top,
  output right_h,
  output left_bt,
  output bt,
  output right_bt
);

  wire and_1_out, and_2_out, and_3_out, and_4_out, and_5_out, and_6_out, and_7_out, and_8_out, and_9_out,
       and_10_out, and_11_out, and_12_out, and_13_out, and_14_out, and_15_out, and_16_out, and_17_out,
       and_18_out, and_19_out, and_20_out, and_21_out, and_22_out, and_23_out, and_24_out, and_25_out,
       and_26_out, and_27_out, not_1_out, not_2_out, not_3_out, not_4_out, not_5_out, not_6_out, not_7_out,
       not_8_out, not_9_out, not_10_out, not_11_out, not_12_out, not_13_out, not_14_out, not_15_out,
       not_16_out, not_17_out, not_18_out, not_19_out, not_20_out, not_21_out, not_22_out, not_23_out,
       not_24_out, not_25_out, not_26_out, not_27_out, not_28_out, not_29_out, not_30_out, not_31_out,
       not_32_out, not_33_out, not_34_out, not_35_out, not_36_out, not_37_out, not_38_out, not_39_out,
       not_40_out, not_41_out, not_42_out, not_43_out, not_44_out, not_45_out, not_46_out, not_47_out;

  not not_1 (not_1_out, A);
  not not_2 (not_2_out, B);
  not not_3 (not_3_out, D);
  not not_4 (not_4_out, C);
  not not_5 (not_5_out, D);
  not not_6 (not_6_out, B);
  not not_7 (not_7_out, C);
  not not_8 (not_8_out, B);
  not not_9 (not_9_out, A);
  not not_10 (not_10_out, B);
  and and_1 (and_1_out, not_9_out, not_10_out, C);
  not not_11 (not_11_out, A);
  and and_2 (and_2_out, not_11_out, B, not_12_out);
  not not_12 (not_12_out, C);
  not not_13 (not_13_out, B);
  and and_3 (and_3_out, A, not_13_out, not_14_out);
  not not_14 (not_14_out, C);
  and and_4 (and_4_out, A, not_15_out, not_16_out);
  not not_15 (not_15_out, B);
  not not_16 (not_16_out, D);
  not not_17 (not_17_out, A);
  not not_18 (not_18_out, B);
  and and_5 (and_5_out, not_17_out, not_18_out, C);
  not not_19 (not_19_out, A);
  and and_6 (and_6_out, not_19_out, B, not_20_out);
  not not_20 (not_20_out, C);
  and and_7 (and_7_out, A, not_21_out, not_22_out);
  not not_21 (not_21_out, B);
  not not_22 (not_22_out, C);
  not not_23 (not_23_out, B);
  and and_8 (and_8_out, A, not_23_out, not_24_out);
  not not_24 (not_24_out, D);
  not not_25 (not_25_out, A);
  and and_9 (and_9_out, not_25_out, D);
  not not_26 (not_26_out, A);
  and and_10 (and_10_out, not_26_out, B);
  not not_27 (not_27_out, B);
  and and_11 (and_11_out, A, not_27_out, not_28_out);
  not not_28 (not_28_out, D);
  and and_12 (and_12_out, A, not_29_out, not_30_out);
  not not_29 (not_29_out, C);
  not not_30 (not_30_out, D);
  not not_31 (not_31_out, B);
  and and_13 (and_13_out, not_31_out, C);
  not not_32 (not_32_out, A);
  and and_14 (and_14_out, not_32_out, B, not_33_out);
  not not_33 (not_33_out, C);
  not not_34 (not_34_out, C);
  and and_15 (and_15_out, A, not_34_out, not_35_out);
  not not_35 (not_35_out, D);
  not not_36 (not_36_out, B);
  not not_37 (not_37_out, C);
  not not_38 (not_38_out, A);
  not not_39 (not_39_out, B);
  not not_40 (not_40_out, D);
  not not_41 (not_41_out, C);
  not not_42 (not_42_out, D);
  not not_43 (not_43_out, A);
  and and_16 (and_16_out, not_43_out, D);
  not not_44 (not_44_out, A);
  and and_17 (and_17_out, not_44_out, B);
  and and_18 (and_18_out, A, not_45_out);
  not not_45 (not_45_out, B);
  not not_46 (not_46_out, C);
  and and_19 (and_19_out, A, not_46_out, not_47_out);
  not not_47 (not_47_out, D);
  and and_20 (and_20_out, not_1_out, not_2_out, C, not_3_out);
  and and_21 (and_21_out, B, not_4_out, not_5_out);
  and and_22 (and_22_out, A, not_6_out, not_7_out);
  and and_23 (and_23_out, A, not_8_out, D);
  or or_1 (left_h, and_1_out, and_2_out, and_3_out, and_4_out);
  or or_2 (top, and_5_out, and_6_out, and_7_out, and_8_out);
  or or_3 (right_h, and_9_out, and_10_out, and_11_out, and_12_out);
  or or_4 (left_bt, and_13_out, and_14_out, and_15_out);
  and and_24 (and_24_out, not_36_out, not_37_out, D);
  and and_25 (and_25_out, not_38_out, B, C);
  and and_26 (and_26_out, A, not_39_out, C, not_40_out);
  and and_27 (and_27_out, A, B, not_41_out, not_42_out);
  or or_5 (right_bt, and_16_out, and_17_out, and_18_out, and_19_out);
  or or_6 (cnt, and_20_out, and_21_out, and_22_out, and_23_out);
  or or_7 (bt, and_24_out, and_25_out, and_26_out, and_27_out);
endmodule

module thd_letter (
  input  A,
  input  B,
  input  C,
  input  D,
  output cnt,
  output left_h,
  output top,
  output right_h,
  output left_bottom,
  output bt,
  output right_bt
);

  wire and_1_out, and_2_out, and_3_out, and_4_out, and_5_out, and_6_out, and_7_out, and_8_out, and_9_out,
       and_10_out, and_11_out, and_12_out, and_13_out, and_14_out, and_15_out, and_16_out, and_17_out,
       and_18_out, and_19_out, and_20_out, and_21_out, and_22_out, and_23_out, and_24_out, and_25_out,
       not_1_out, not_2_out, not_3_out, not_4_out, not_5_out, not_6_out, not_7_out, not_8_out, not_9_out,
       not_10_out, not_11_out, not_12_out, not_13_out, not_14_out, not_15_out, not_16_out, not_17_out,
       not_18_out, not_19_out, not_20_out, not_21_out, not_22_out, not_23_out, not_24_out, not_25_out,
       not_26_out, not_27_out, not_28_out, not_29_out, not_30_out, not_31_out, not_32_out, not_33_out,
       not_34_out, not_35_out, not_36_out, not_37_out, not_38_out, not_39_out, not_40_out;

  not not_1 (not_1_out, C);
  and and_1 (and_1_out, not_1_out, D);
  not not_2 (not_2_out, A);
  and and_2 (and_2_out, not_2_out, C, not_3_out);
  not not_3 (not_3_out, D);
  not not_4 (not_4_out, B);
  and and_3 (and_3_out, A, not_4_out, not_5_out);
  not not_5 (not_5_out, D);
  not not_6 (not_6_out, B);
  and and_4 (and_4_out, not_6_out, C);
  not not_7 (not_7_out, A);
  and and_5 (and_5_out, not_7_out, B, not_8_out);
  not not_8 (not_8_out, C);
  not not_9 (not_9_out, A);
  and and_6 (and_6_out, not_9_out, B, D);
  and and_7 (and_7_out, A, not_10_out);
  not not_10 (not_10_out, B);
  and and_8 (and_8_out, A, not_11_out, not_12_out);
  not not_11 (not_11_out, C);
  not not_12 (not_12_out, D);
  not not_13 (not_13_out, A);
  not not_14 (not_14_out, B);
  not not_15 (not_15_out, C);
  not not_16 (not_16_out, D);
  not not_17 (not_17_out, B);
  not not_18 (not_18_out, C);
  not not_19 (not_19_out, A);
  not not_20 (not_20_out, C);
  not not_21 (not_21_out, B);
  not not_22 (not_22_out, B);
  and and_9 (and_9_out, not_22_out, D);
  not not_23 (not_23_out, A);
  and and_10 (and_10_out, not_23_out, C);
  not not_24 (not_24_out, C);
  and and_11 (and_11_out, B, not_24_out, not_25_out);
  not not_25 (not_25_out, D);
  and and_12 (and_12_out, A, not_26_out);
  not not_26 (not_26_out, B);
  not not_27 (not_27_out, B);
  and and_13 (and_13_out, not_27_out, C, not_28_out);
  not not_28 (not_28_out, D);
  not not_29 (not_29_out, A);
  and and_14 (and_14_out, not_29_out, B, D);
  and and_15 (and_15_out, A, not_30_out, not_31_out);
  not not_30 (not_30_out, C);
  not not_31 (not_31_out, D);
  not not_32 (not_32_out, B);
  and and_16 (and_16_out, A, not_32_out, C);
  not not_33 (not_33_out, A);
  not not_34 (not_34_out, C);
  not not_35 (not_35_out, A);
  not not_36 (not_36_out, D);
  not not_37 (not_37_out, B);
  not not_38 (not_38_out, C);
  not not_39 (not_39_out, D);
  not not_40 (not_40_out, B);
  or or_1 (cnt, and_1_out, and_2_out, and_3_out);
  or or_2 (left_h, and_4_out, and_5_out, and_6_out, and_7_out, and_8_out);
  and and_17 (and_17_out, not_13_out, not_14_out, C, D);
  or or_3 (top, and_17_out, and_18_out, and_19_out);
  and and_18 (and_18_out, B, not_15_out, not_16_out);
  and and_19 (and_19_out, A, not_17_out, not_18_out);
  and and_20 (and_20_out, not_19_out, B, not_20_out, D);
  or or_4 (right_h, and_20_out, and_21_out);
  and and_21 (and_21_out, A, not_21_out, D);
  or or_5 (left_bottom, and_9_out, and_10_out, and_11_out, and_12_out);
  or or_6 (bt, and_13_out, and_14_out, and_15_out, and_16_out);
  and and_22 (and_22_out, not_33_out, not_34_out, D);
  and and_23 (and_23_out, not_35_out, C, not_36_out);
  and and_24 (and_24_out, A, not_37_out, not_38_out, not_39_out);
  and and_25 (and_25_out, A, not_40_out, C, D);
  or or_7 (right_bt, and_22_out, and_23_out, and_24_out, and_25_out);
endmodule

module month_display (
  input  in_1
);

  wire clock_1_out, fst_letter_1_bt, fst_letter_1_cnt, fst_letter_1_left_bt, fst_letter_1_left_h,
       fst_letter_1_right_bt, fst_letter_1_right_h, fst_letter_1_top, mid_letter_1_bt, mid_letter_1_cnt,
       mid_letter_1_left_bt, mid_letter_1_lft_high, mid_letter_1_right_bt, mid_letter_1_right_h,
       mid_letter_1_top, thd_letter_1_bt, thd_letter_1_cnt, thd_letter_1_left_bottom, thd_letter_1_left_h,
       thd_letter_1_right_bt, thd_letter_1_right_h, thd_letter_1_top;
  wire [3:0] better_dm_1_mth_output;

  Clock clock_1 (.out(clock_1_out));
  better_dm better_dm_1 (
    .enable(in_1), .enable_test(in_1), .CLK_input(clock_1_out), .mth_output(better_dm_1_mth_output));  // open: nxt_dig
  fst_letter fst_letter_1 (
    .A(better_dm_1_mth_output[3]), .B(better_dm_1_mth_output[2]), .C(better_dm_1_mth_output[1]),
    .D(better_dm_1_mth_output[0]), .cnt(fst_letter_1_cnt), .left_h(fst_letter_1_left_h),
    .top(fst_letter_1_top), .right_h(fst_letter_1_right_h), .left_bt(fst_letter_1_left_bt),
    .bt(fst_letter_1_bt), .right_bt(fst_letter_1_right_bt));
  mid_letter mid_letter_1 (
    .A(better_dm_1_mth_output[3]), .B(better_dm_1_mth_output[2]), .C(better_dm_1_mth_output[1]),
    .D(better_dm_1_mth_output[0]), .cnt(mid_letter_1_cnt), .lft_high(mid_letter_1_lft_high),
    .top(mid_letter_1_top), .right_h(mid_letter_1_right_h), .left_bt(mid_letter_1_left_bt),
    .bt(mid_letter_1_bt), .right_bt(mid_letter_1_right_bt));
  thd_letter thd_letter_1 (
    .A(better_dm_1_mth_output[3]), .B(better_dm_1_mth_output[2]), .C(better_dm_1_mth_output[1]),
    .D(better_dm_1_mth_output[0]), .cnt(thd_letter_1_cnt), .left_h(thd_letter_1_left_h),
    .top(thd_letter_1_top), .right_h(thd_letter_1_right_h), .left_bottom(thd_letter_1_left_bottom),
    .bt(thd_letter_1_bt), .right_bt(thd_letter_1_right_bt));
  _7_Segment_Display u_7_segment_display_1 (
    .g(fst_letter_1_cnt), .f(fst_letter_1_left_h), .a(fst_letter_1_top), .b(fst_letter_1_right_h),
    .e(fst_letter_1_left_bt), .d(fst_letter_1_bt), .c(fst_letter_1_right_bt));  // open: dp
  _7_Segment_Display u_7_segment_display_2 (
    .g(mid_letter_1_cnt), .f(mid_letter_1_lft_high), .a(mid_letter_1_top), .b(mid_letter_1_right_h),
    .e(mid_letter_1_left_bt), .d(mid_letter_1_bt), .c(mid_letter_1_right_bt));  // open: dp
  _7_Segment_Display u_7_segment_display_3 (
    .g(thd_letter_1_cnt), .f(thd_letter_1_left_h), .a(thd_letter_1_top), .b(thd_letter_1_right_h),
    .e(thd_letter_1_left_bottom), .d(thd_letter_1_bt), .c(thd_letter_1_right_bt));  // open: dp

  // Notes on the sheet:
  //   mettre janvier par défaut
  //   : regarder les cas nuls et faire un reset à ce moment là
endmodule

module better_dm (
  input  enable,
  input  enable_test,
  input  CLK_input,
  input  nxt_dig,
  output [3:0] mth_output
);

  wire and_6_out, and_7_out, en_j2, en_m1, en_m2, fixer, month_lgth_1_f, not_1_out, not_2_out, not_3_out,
       not_4_out, not_5_out, or_1_out, or_2_out, reset_30, rs_j1, rs_j2, rs_j2_p;
  wire [3:0] add_4_bits_2_out_put;
  wire [3:1] add_4_bits_1_out_put;

  date date_1 (.set_mode(enable), .CLK_input(CLK_input), .next_digit(nxt_dig));  // open: but_in, nv_jour
  or or_1 (or_1_out, rs_j1, rs_j2, reset_30);
  or or_2 (or_2_out, rs_j2, reset_30, rs_j2_p);
  add_4_bits add_4_bits_1 (
    .enable(enable_test), .CLK_input(CLK_input), .Reset(or_1_out), .out_put({add_4_bits_1_out_put, en_m1}));
  add_4_bits add_4_bits_2 (.enable(en_j2), .CLK_input(CLK_input), .Reset(or_2_out), .out_put(add_4_bits_2_out_put));
  add_4_bits add_4_bits_3 (.enable(en_m2), .CLK_input(CLK_input), .out_put(mth_output));  // open: Reset
  and and_1 (en_j2, en_m1, add_4_bits_1_out_put[3]);
  and and_2 (rs_j1, add_4_bits_1_out_put[1], add_4_bits_1_out_put[3]);
  not not_1 (not_1_out, add_4_bits_1_out_put[3]);
  and and_3 (fixer, add_4_bits_2_out_put[0], add_4_bits_2_out_put[1]);
  month_lgth month_lgth_1 (
    .A(mth_output[0]), .B(mth_output[1]), .C(mth_output[2]), .D(mth_output[3]), .f(month_lgth_1_f));
  and cl_31 (rs_j2, add_4_bits_1_out_put[1], not_1_out, fixer);
  and and_4 (rs_j2_p, en_m1, fixer, not_2_out);
  not not_2 (not_2_out, month_lgth_1_f);
  not not_3 (not_3_out, month_lgth_1_f);
  and and_5 (reset_30, not_3_out, fixer, en_m1);
  Hex_Digit_Display hex_digit_display_1 (.value({add_4_bits_1_out_put, en_m1}));  // open: dp
  Hex_Digit_Display hex_digit_display_2 (.value(add_4_bits_2_out_put));  // open: dp
  and and_6 (and_6_out, fixer, not_4_out, not_5_out);
  not not_4 (not_4_out, en_m1);
  not not_5 (not_5_out, month_lgth_1_f);
  and and_7 (and_7_out, en_m1, fixer, month_lgth_1_f);
  or or_3 (en_m2, and_6_out, and_7_out);

  // Other names for the same wires on the sheet: one_j1 = en_m1; CLK = CLK_input

  // Notes on the sheet:
  //   ADD FEBRUARY
endmodule

module month_lgth (
  input  A,
  input  B,
  input  C,
  input  D,
  output f
);

  wire and_1_out, and_2_out, and_3_out, not_1_out, not_2_out;

  not not_1 (not_1_out, A);
  and and_1 (and_1_out, not_1_out, not_2_out);
  not not_2 (not_2_out, D);
  and and_2 (and_2_out, B, C);
  and and_3 (and_3_out, A, D);
  or or_1 (f, and_1_out, and_2_out, and_3_out);
endmodule

module hours_conditions (
  input  [3:0] wk_hours_input,
  input  [3:0] st_hours_input,
  output reset_impulse
);

  wire and_1_out, and_2_out, and_3_out, and_4_out, and_5_out, and_6_out, and_7_out, and_8_out, not_1_out,
       not_2_out, not_3_out, not_4_out, not_5_out, not_6_out, not_7_out, not_8_out, not_9_out, not_10_out,
       not_11_out, not_12_out;

  not not_1 (not_1_out, wk_hours_input[1]);
  not not_2 (not_2_out, wk_hours_input[2]);
  not not_3 (not_3_out, wk_hours_input[3]);
  not not_4 (not_4_out, wk_hours_input[0]);
  not not_5 (not_5_out, wk_hours_input[2]);
  not not_6 (not_6_out, wk_hours_input[3]);
  not not_7 (not_7_out, wk_hours_input[2]);
  not not_8 (not_8_out, wk_hours_input[2]);
  not not_9 (not_9_out, wk_hours_input[0]);
  and and_1 (and_1_out, not_9_out, not_10_out, not_11_out, not_12_out);
  not not_10 (not_10_out, wk_hours_input[1]);
  not not_11 (not_11_out, wk_hours_input[2]);
  not not_12 (not_12_out, wk_hours_input[2]);
  and and_2 (and_2_out, wk_hours_input[0], wk_hours_input[0], not_2_out, not_3_out);
  and and_3 (and_3_out, wk_hours_input[1], not_4_out, not_5_out, not_6_out);
  and and_4 (and_4_out, wk_hours_input[0], wk_hours_input[1], not_7_out, not_8_out);
  and and_5 (and_5_out, and_2_out, st_hours_input[1]);
  and and_6 (and_6_out, and_3_out, st_hours_input[1]);
  and and_7 (and_7_out, and_4_out, st_hours_input[1]);
  and and_8 (and_8_out, and_1_out, st_hours_input[1]);
  or or_1 (reset_impulse, and_5_out, and_6_out, and_7_out, and_8_out);

  // Other names for the same wires on the sheet: one = wk_hours_input[0]; two = wk_hours_input[1];
  //   four = wk_hours_input[2]; three = wk_hours_input[2]
endmodule
